# Fritzing sketch HallEffectSensor (saved by Fritzing 0.9.3b)
breadboards: 1

parts:
  U1 = lolin
  R1 = Resistor [tolerance=±5% resistance=220 package=THT]

nets:
  N1: U1.connector18, R1.Pin_1
  N2: U1.connector37, R1.Pin_0
