# Fritzing sketch SingleButton (saved by Fritzing 0.9.3b)
breadboards: 1

parts:
  U1 = lolin
  S1 = Pushbutton [package="[THT]"]
  R1 = Resistor [tolerance=±5% resistance=10k package=THT]

nets:
  N1: U1.connector0, S1.Pin_1, S1.Pin_2, R1.Pin_0
  N2: U1.connector2, S1.Pin_3, S1.Pin_4
  N3: U1.connector37, R1.Pin_1

// code stored in the sketch: CapacitiveTouch.ino
/*
This is un example howto use Touch Intrrerupts
The bigger the threshold, the more sensible is the touch
*/

#include <WiFi.h>
#include <PubSubClient.h>

const char* SSID="ASUS";
const char* PASS="MEGA SHED";
const char* MQTT="10.10.11.3";
const char* TOPIC="status/touch/";
WiFiClient espWifi;
PubSubClient client(espWifi);

int threshold = 40;
bool touch0detected = false;
bool touch1detected = false;
bool touch2detected = false;

void gotTouch0(){
 touch0detected = true;
}

void gotTouch1(){
 touch1detected = true;
}

void gotTouch2(){
 touch2detected = true;
}

void setup() {
  Serial.begin(115200);
  setup_wifi();
  delay(1000); // give me time to bring up serial monitor
  client.setServer(MQTT, 1883);
  
  Serial.println("ESP32 Touch Interrupt Test");
  touchAttachInterrupt(T0, gotTouch0, threshold);
//  touchAttachInterrupt(T1, gotTouch1, threshold); // Attached to the reset button, so won't work as capacitive
  touchAttachInterrupt(T2, gotTouch2, threshold);
}

void loop(){
  mqtt();

  if(touch0detected){
    touch0detected = false;
    Serial.printf("Touch 0 (pin %d) detected\n", T0);
    client.publish("status/esp32/touch", "0");
  }
  if(touch1detected){
    touch1detected = false;
    Serial.printf("Touch 1 (pin %d) detected\n", T1);
    client.publish("status/esp32/touch", "2");
  }
  if(touch2detected){
    touch2detected = false;
    Serial.printf("Touch 2 (pin %d) detected\n", T2);
    client.publish("status/esp32/touch", "2");
  }
  Serial.printf("w %d, %d, %d, %d, %d, %d, %d, %d, %d, %d\n", touchRead(T0), touchRead(T1), touchRead(T2), touchRead(T3), touchRead(T4), touchRead(T5), touchRead(T6), touchRead(T7), touchRead(T8), touchRead(T9));  // get value using T0
  delay(1000);
}

void mqtt() {
  while (!client.connected()) {
    client.connect("testesp32");
    Serial.println("+");
  }
  client.loop();
}

void setup_wifi() {
  delay(10);
  WiFi.begin(SSID, PASS);
  while (WiFi.status() != WL_CONNECTED) {
    Serial.println(".");
    delay(500);
  }
  Serial.println("Connected:");
  Serial.println( WiFi.localIP());
}

// code stored in the sketch: SingleButton.ino
/*
  Button

  Turns on and off a light emitting diode(LED) connected to digital pin 13,
  when pressing a pushbutton attached to pin 2.

  The circuit:
  - LED attached from pin 13 to ground
  - pushbutton attached to pin 2 from +5V
  - 10K resistor attached to pin 2 from ground

  - Note: on most Arduinos there is already an LED on the board
    attached to pin 13.

  created 2005
  by DojoDave <http://www.0j0.org>
  modified 30 Aug 2011
  by Tom Igoe

  This example code is in the public domain.

  http://www.arduino.cc/en/Tutorial/Button
*/

// constants won't change. They're used here to set pin numbers:
const int buttonPin = 36;     // the number of the pushbutton pin
const int ledPin =  BUILTIN_LED;      // the number of the LED pin

// variables will change:
int buttonState = 0;         // variable for reading the pushbutton status

void setup() {
  // initialize the LED pin as an output:
  pinMode(ledPin, OUTPUT);
  // initialize the pushbutton pin as an input:
  pinMode(buttonPin, INPUT);
}

void loop() {
  // read the state of the pushbutton value:
  buttonState = digitalRead(buttonPin);

  // check if the pushbutton is pressed. If it is, the buttonState is HIGH:
  if (buttonState == HIGH) {
    // turn LED on:
    digitalWrite(ledPin, HIGH);
  } else {
    // turn LED off:
    digitalWrite(ledPin, LOW);
  }
}
