# Fritzing sketch Sweep_esp32 (saved by Fritzing 0.9.3b)
breadboards: 1

parts:
  U1 = lolin
  BATT1 = 4xAA Switchable Battery Pack w/JST connector
  J1 = Basic Servo
  R1 = Resistor [tolerance=±5% resistance=220 package=THT]

nets:
  N1: U1.connector20, BATT1.NEG, J1.gnd
  N2: U1.connector33, R1.Pin_0
  N3: BATT1.POS, J1.vcc
  N4: J1.pulse, R1.Pin_1

custom parts:
  4xAA Switchable Battery Pack w/JST connector: 4xAA Switchable Battery Pack with JST connector
